# Fritzing sketch Version1 (saved by Fritzing 0.9.3b)

parts:
  e-radionica_com2 = LM393 LDR breakout [part_number=100027]
  Mod2 = Raspberry Pi 4B
  BH1750FVI_GY-3 = BH1750FVI GY-30 Digital Light Sensor Module [part_number="BH1750FVI GY-30"]
  Part2 = HC-SR501 Body Sensor Module
  U5 = LM2596 step down module
  M4 = Osoyoo SX1278-ra-02  # not connected
  M5 = Osoyoo SX1278-ra-02
  U7 = Voltage Regulator -- 3.3 V -- LM1117

nets:
  VCC: e-radionica_com2.VCC, BH1750FVI_GY-3.VCC, Part2.VCC, U5.OUT+
  GND: e-radionica_com2.GND, Mod2.GND, BH1750FVI_GY-3.SCL, Part2.GND, U5.IN-, U5.OUT-, M5.GND, U7.GND
  N1: e-radionica_com2.DO, Mod2.GPIO26
  N2: Mod2.GPIO2, BH1750FVI_GY-3.SDA
  N3: Mod2.GPIO3, BH1750FVI_GY-3.INT
  N4: Mod2.GPIO27, Part2.OUT
  N5: Mod2.GPIO22, M5.NSS
  N6: Mod2.GPIO24, M5.DIO0
  N7: Mod2.GPIO10, M5.MOSI
  N8: Mod2.GPIO9, M5.MISO
  N9: Mod2.GPIO25, M5.RST
  N10: Mod2.GPIO11, M5.SCK
  N11: M5.3.3V, U7.OUT

custom parts:
  BH1750FVI GY-30 Digital Light Sensor Module: BH1750FVI GY-30 Digital Light Sensor Module BH1750FVI is a digital Ambient Light Sensor IC for I²C bus interface. This IC is the most suitable to obtain the ambient light data for adjusting LCD and keypad backlight power of mobile phone. It is possible to detect wide range at High resolution (1 - 65535 lx).
  HC-SR501 Body Sensor Module: Pyroelectric Infrared PIR Motion Sensor Detector Module
  LM2596 step down module: LM2596 DC-DC step down power supply module 3 A.
  Osoyoo SX1278-ra-02: Osoyoo Long Distance wireless transceiver Uart LoRa Module.
  Voltage Regulator -- 3.3 V -- LM1117: LM1117-3.3 Voltage regulator, 3.3 V output. Note that the pinout order is not the same as LM7805 or LM7833.
