# Fritzing sketch LightSensor (saved by Fritzing 0.9.3b)

parts:
  Mod1 = Raspberry Pi 4B
  BH1750FVI_GY-1 = BH1750FVI GY-30 Digital Light Sensor Module [part_number="BH1750FVI GY-30"]
  U1 = LM2596 step down module

nets:
  N1: Mod1.GPIO2, BH1750FVI_GY-1.SDA
  N2: Mod1.GPIO3, BH1750FVI_GY-1.INT
  N3: Mod1.GND, BH1750FVI_GY-1.SCL, U1.OUT-
  N4: BH1750FVI_GY-1.VCC, U1.OUT+

custom parts:
  BH1750FVI GY-30 Digital Light Sensor Module: BH1750FVI GY-30 Digital Light Sensor Module BH1750FVI is a digital Ambient Light Sensor IC for I²C bus interface. This IC is the most suitable to obtain the ambient light data for adjusting LCD and keypad backlight power of mobile phone. It is possible to detect wide range at High resolution (1 - 65535 lx).
  LM2596 step down module: LM2596 DC-DC step down power supply module 3 A.
