# Fritzing sketch LoRa (saved by Fritzing 0.9.3b)

parts:
  M1 = Osoyoo SX1278-ra-02
  Mod1 = Raspberry Pi 4B

nets:
  N1: M1.RST, Mod1.GPIO25
  N2: M1.DIO0, Mod1.GPIO24
  GND: M1.GND, Mod1.GND
  N3: M1.SCK, Mod1.GPIO11
  N4: M1.MISO, Mod1.GPIO9
  N5: M1.MOSI, Mod1.GPIO10
  N6: M1.NSS, Mod1.GPIO22

custom parts:
  Osoyoo SX1278-ra-02: Osoyoo Long Distance wireless transceiver Uart LoRa Module.
