# Fritzing sketch PIRSensor (saved by Fritzing 0.9.3b)

parts:
  Mod1 = Raspberry Pi 4B
  Part1 = HC-SR501 Body Sensor Module
  U1 = LM2596 step down module

nets:
  GND: Mod1.GND, Part1.GND, U1.IN-, U1.OUT-
  N1: Mod1.GPIO27, Part1.VCC, Part1.OUT, U1.OUT+

custom parts:
  HC-SR501 Body Sensor Module: Pyroelectric Infrared PIR Motion Sensor Detector Module
  LM2596 step down module: LM2596 DC-DC step down power supply module 3 A.
