# Fritzing sketch Version2 (saved by Fritzing 0.9.3b)

parts:
  e-radionica_com3 = LM393 LDR breakout [part_number=100027]
  M6 = Osoyoo SX1278-ra-02  # not connected
  U8 = LM2596 step down module
  Mod3 = Raspberry Pi 4B
  BH1750FVI_GY-5 = BH1750FVI GY-30 Digital Light Sensor Module [part_number="BH1750FVI GY-30"]
  M8 = Osoyoo SX1278-ra-02
  U10 = Voltage Regulator -- 3.3 V -- LM1117
  Part4 = HC-SR501 Body Sensor Module

nets:
  VCC: e-radionica_com3.VCC, U8.OUT+, BH1750FVI_GY-5.VCC, U10.IN, Part4.VCC
  GND: e-radionica_com3.GND, U8.IN-, U8.OUT-, Mod3.GND, BH1750FVI_GY-5.SCL, M8.GND, U10.GND, Part4.GND
  N1: e-radionica_com3.DO, Mod3.GPIO26
  N2: Mod3.GPIO2, BH1750FVI_GY-5.SDA
  N3: Mod3.GPIO3, BH1750FVI_GY-5.INT
  N4: Mod3.GPIO4, M8.RST
  N5: Mod3.GPIO17, M8.DIO0
  N6: Mod3.GPIO22, M8.NSS
  N7: Mod3.GPIO10, M8.MOSI
  N8: Mod3.GPIO9, M8.MISO
  N9: Mod3.GPIO11, M8.SCK
  N10: Mod3.GPIO16, Part4.OUT
  N11: M8.3.3V, U10.OUT

custom parts:
  Osoyoo SX1278-ra-02: Osoyoo Long Distance wireless transceiver Uart LoRa Module.
  LM2596 step down module: LM2596 DC-DC step down power supply module 3 A.
  BH1750FVI GY-30 Digital Light Sensor Module: BH1750FVI GY-30 Digital Light Sensor Module BH1750FVI is a digital Ambient Light Sensor IC for I²C bus interface. This IC is the most suitable to obtain the ambient light data for adjusting LCD and keypad backlight power of mobile phone. It is possible to detect wide range at High resolution (1 - 65535 lx).
  Voltage Regulator -- 3.3 V -- LM1117: LM1117-3.3 Voltage regulator, 3.3 V output. Note that the pinout order is not the same as LM7805 or LM7833.
  HC-SR501 Body Sensor Module: Pyroelectric Infrared PIR Motion Sensor Detector Module
