# Fritzing sketch failure_schem (saved by Fritzing 0.9.3b)
breadboards: 1

parts:
  R1 = Resistor [tolerance=±5% resistance=220 package=THT]
  U1 = Optocoupler [package=THT]
  D1 = Rectifier Diode [part_number=1N4001 package="300 mil [THT]"]

nets:
  lamp+: R1.Pin_0
  N1: R1.Pin_1, U1.Pin_1, D1.cathode
  lamp-: U1.Pin_2, D1.anode
  GND: U1.Pin_4
  5V/GPIO: U1.Pin_5
